# Fritzing sketch HomePrototypeLayout (saved by Fritzing 0.9.3b)
circuit board: 8.46667cm x 5.64444cm
breadboards: 1

parts:
  SCL_Pullup = Resistor [tolerance=±1% resistance=5.1k package=THT]
  Pot = TRIMPOT [package=3386u]
  SDA_Pullup = Resistor [tolerance=±1% resistance=5.1k package=THT]
  LED_Ring = 12 NeoPixel Ring [part_number=1643]
  Sensirion_DP-10cmH2O = DIP - 8 pins [part_number=1223019V5 chip_label="DP Sensor Breakout Board" package="DIP (Dual Inline) [THT]"]
  Feather_32u4_BlueFruit_LE = Adafruit Feather 32u4 Bluefruit [part_number="Adafruit #2829"]
  Power_Switch = Toggle Switch [package=THT]
  Battery = Lithium Ion Polymer Battery 3.7v 500mAh [part_number=1578]
  ~Display_Battery = SWITCH-MOMENTARY-2 [package=tactile-pth]

nets:
  VDD: SCL_Pullup.Pin_0, Pot.CW, SDA_Pullup.Pin_0, LED_Ring.VDD, Sensirion_DP-10cmH2O.VDD, Feather_32u4_BlueFruit_LE.+3V3
  N1: SCL_Pullup.Pin_1, Sensirion_DP-10cmH2O.SCL, Feather_32u4_BlueFruit_LE.3
  GND: Pot.CCW, LED_Ring.GND, Sensirion_DP-10cmH2O.GND, Feather_32u4_BlueFruit_LE.GND, Power_Switch.COM, Battery.negative, ~Display_Battery.1
  N2: Pot.WIPER, Feather_32u4_BlueFruit_LE.A4
  N3: SDA_Pullup.Pin_1, Sensirion_DP-10cmH2O.SDA, Feather_32u4_BlueFruit_LE.2
  N4: LED_Ring.IN, Feather_32u4_BlueFruit_LE.6
  N5: Feather_32u4_BlueFruit_LE.VBAT, Battery.positive
  N6: Feather_32u4_BlueFruit_LE.EN, Power_Switch.L1
  N7: Feather_32u4_BlueFruit_LE.13, ~Display_Battery.2

custom parts:
  12 NeoPixel Ring: 12 ultra bright smart LED NeoPixels are arranged in a circle with 1.5" (37mm) outer diameter. The rings are 'chainable' - connect the output pin of one to the input pin of another. Use only one microcontroller pin to control as many as you can chain together! Each LED is addressable as the driver chip is inside the LED. Each one has ~18mA constant current drive so the color will be very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
  DIP - 8 pins: Sensor SDP31 Breakout board with I2C interface.
  Adafruit Feather 32u4 Bluefruit: This is the Adafruit Feather 32u4 Bluefruit - our take on an 'all-in-one' Arduino-compatible + Bluetooth Low Energy with built in USB and battery charging. Its an Adafruit Feather 32u4 with a BTLE module, ready to rock! We have other boards in the Feather family, check'em out here. Bluetooth Low Energy is the hottest new low-power, 2.4GHz spectrum wireless protocol. In particular, its the only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
  Lithium Ion Polymer Battery 3.7v 500mAh: Lithium ion polymer (also known as 'lipo' or 'lipoly') batteries are thin, light and powerful. The output ranges from 4.2V when completely charged to 3.7V. This battery has a capacity of 500mAh for a total of about 1.9 Wh. The batteries come pre-attached with a genuine 2-pin JST-PH connector as shown and include the necessary protection circuitry.
